# Fritzing sketch policecarconnections (saved by Fritzing 0.9.10b)
breadboards: 1

parts:
  R1 = Resistor [tolerance=±5% power=0.25 resistance=220 package=THT]
  R2 = Resistor [tolerance=±5% power=0.25 resistance=220 package=THT]
  R3 = Resistor [tolerance=±5% power=0.25 resistance=220 package=THT]
  LED1 = LED - 5mm [color="Red (633nm)" current=0.030 package="5 mm [THT]"]
  LED2 = LED - 5mm [color="White (4500K)" current=0.030 package="5 mm [THT]"]
  LED3 = LED - 5mm [color="Blue (525nm)" current=0.030 package="5 mm [THT]"]
  L298N1 = L298N DC motor driver
  M1 = gear-motor
  M2 = gear-motor
  Part1 = Arduino Mega ADK (Rev3)
  VCC1 = Battery block 9V  # not connected
  VCC2 = Battery block 9V
  SP1 = SPEAKER [package=pcb_mount_speaker]
  Part2 = NRF24L01+ Breakout Board
  J1 = Basic Servo

nets:
  N1: R1.Pin_0, LED1.cathode
  GND: R1.Pin_1, R2.Pin_1, R3.Pin_1, Part1.GND, VCC2.-, Part2.GND, J1.gnd
  N2: R2.Pin_0, LED2.cathode
  N3: R3.Pin_0, LED3.cathode
  N4: LED1.anode, Part1.D46
  N5: LED2.anode, Part1.D47
  N6: LED3.anode, Part1.D48
  N7: L298N1.OUT1, M1.pin_2
  N8: L298N1.OUT2, M1.pin_1
  N9: L298N1.OUT4, M2.pin_1
  N10: L298N1.GND, SP1.+
  N11: L298N1.ENA, Part1.D5_PWM
  N12: L298N1.ENB, Part1.D6_PWM
  N13: L298N1.IN1, Part1.D24
  N14: L298N1.IN2, Part1.D22
  N15: L298N1.IN3, Part1.D26
  N16: L298N1.IN4, Part1.D28
  N17: Part1.D9_PWM, Part2.IRQ
  N18: Part1.D8_PWM, Part2.CS
  3V3: Part1.3V3, Part2.VCC
  N19: Part1.D2_PWM, SP1.-
  N20: Part1.D4_PWM, J1.pulse
  N21: Part1.D7_PWM, Part2.CE
  N22: Part1.D50/MISO, Part2.MISO
  N23: Part1.D51/MOSI, Part2.MOSI
  N24: Part1.D52/SCK, Part2.SCK

custom parts:
  L298N DC motor driver: 2x DC motor driver with 78M05 positive voltage regulator (7..35 V) L298N: max 46 V, 2 A Set 5 V Enable jumper to enable 5 V regultor (needed for the L298N) and +5 V output at screw terminal or supply external +5 V at screw terminal Set ENA and/or ENB to +5 V to enable motor permanently or supply ENA and/or ENB with PWM signal IN1 and IN2 set rotation directory for motor A (OUT1/OUT2) IN2 and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
